# Fritzing sketch Uno_2LED (saved by Fritzing 0.9.3b)
breadboards: 1

parts:
  Arduino = Arduino Uno (Rev3)
  LED1 = LED - 5mm [color="Red (633nm)" package="5 mm [THT]"]
  R2 = Resistor [tolerance=±5% resistance=220 package=THT]
  LED2 = LED - 5mm [color="Red (633nm)" package="5 mm [THT]"]
  R3 = Resistor [tolerance=±5% resistance=220 package=THT]

nets:
  N1: Arduino.D12/MISO, R3.Pin_0
  N2: Arduino.D13/SCK, R2.Pin_0
  N3: Arduino.GND, LED1.cathode, LED2.cathode
  N4: LED1.anode, R2.Pin_1
  N5: LED2.anode, R3.Pin_1
