# Fritzing sketch 01_17_HC-06_LED_bb (saved by Fritzing 0.9.10b)
breadboards: 1

parts:
  Onderdeel2 = Arduino Uno (Rev3)
  BT1 = Bluetooth HC-06u [package=THT]
  R1 = Resistor [tolerance=±5% power=0.25 resistance=220 package=THT]  # not connected
  LED1 = LED - 5mm [color="Red (633nm)" current=0.030 package="5 mm [THT]"]
  LED2 = LED - 5mm [color="Green (565nm)" current=0.030 package="5 mm [THT]"]
  R2 = Resistor [tolerance=±5% power=0.25 resistance=220 package=THT]

nets:
  N1: Onderdeel2.D2, BT1.TXD
  N2: Onderdeel2.D3_PWM, BT1.RXD
  N3: Onderdeel2.D6_PWM, R2.Pin_0
  5V: Onderdeel2.5V, BT1.VCC
  GND: Onderdeel2.GND, BT1.GND, LED1.cathode, LED2.cathode
  N4: LED2.anode, R2.Pin_1

custom parts:
  Bluetooth HC-06u: Bluetooth HC-06 - face up, pins down 16.5mm x 37.5mm PCB
