# Fritzing sketch 01_18_ESP8266_wire (saved by Fritzing 0.9.10b)

parts:
  Onderdeel2 = Arduino Uno (Rev3)
  BT1 = Bluetooth HC-06u [package=THT]

nets:
  N1: Onderdeel2.D2, BT1.TXD
  N2: Onderdeel2.D3_PWM, BT1.RXD
  5V: Onderdeel2.5V, BT1.VCC
  GND: Onderdeel2.GND, BT1.GND

custom parts:
  Bluetooth HC-06u: Bluetooth HC-06 - face up, pins down 16.5mm x 37.5mm PCB
