# Fritzing sketch LED_RGB_ON_OFF (saved by Fritzing 0.9.9b)
breadboards: 1

parts:
  Arduino = Arduino Uno (Rev3)
  LED1 = LED - 5mm [color="Red (633nm)" current=0.030 package="5 mm [THT]"]
  R2 = Resistor [tolerance=±5% resistance=220 power=0.25 package=THT]
  LED2 = LED - 5mm [color="Green (560nm)" current=0.030 package="5 mm [THT]"]
  R3 = Resistor [tolerance=±5% resistance=220 power=0.25 package=THT]
  LED3 = LED - 5mm [color="Blue (470nm)" current=0.030 package="5 mm [THT]"]
  R5 = Resistor [tolerance=±5% resistance=220 power=0.25 package=THT]

nets:
  N1: Arduino.D11_PWM/MOSI, R5.Pin_0
  N2: Arduino.D12/MISO, R3.Pin_0
  N3: Arduino.D13/SCK, R2.Pin_0
  N4: Arduino.GND, LED1.cathode, LED2.cathode, LED3.cathode
  N5: LED1.anode, R2.Pin_1
  N6: LED2.anode, R3.Pin_1
  N7: LED3.anode, R5.Pin_1
