# Fritzing sketch _01_02_RGBLed (saved by Fritzing 0.9.9b)
breadboards: 1

parts:
  Arduino = Arduino Uno (Rev3)
  R2 = Resistor [tolerance=±5% resistance=220 power=0.25 package=THT]
  R3 = Resistor [tolerance=±5% resistance=220 power=0.25 package=THT]
  R5 = Resistor [tolerance=±5% resistance=220 power=0.25 package=THT]
  LED4 = RGB LED (com. cathode, rgb) [package="5 mm [THT]"]

nets:
  N1: Arduino.D11_PWM/MOSI, R5.Pin_0
  N2: Arduino.D12/MISO, R3.Pin_0
  N3: Arduino.D13/SCK, R2.Pin_0
  N4: Arduino.GND, LED4.common_cathode
  N5: R2.Pin_1, LED4.red_anode
  N6: R3.Pin_1, LED4.green_anode
  N7: R5.Pin_1, LED4.blue_anode
