# Fritzing sketch _01_02_RGBLed_module (saved by Fritzing 0.9.9b)
breadboards: 1

parts:
  Arduino = Arduino Uno (Rev3)
  Mod2 = KY-016 RGB Full Color LED Module [package="Breakout board"]

nets:
  N1: Arduino.D11_PWM/MOSI, Mod2.B
  N2: Arduino.D12/MISO, Mod2.G
  N3: Arduino.D13/SCK, Mod2.R
  N4: Arduino.GND, Mod2.-

custom parts:
  KY-016 RGB Full Color LED Module: KY-016 Arduino full color 5mm RGB LED, different colors can be obtained by mixing the three primary colors.
