# Fritzing sketch _01_04_read_Button (saved by Fritzing 0.9.9b)
breadboards: 1

parts:
  Arduino = Arduino Uno (Rev3)
  LED1 = LED - 5mm [color="Red (633nm)" current=0.030 package="5 mm [THT]"]
  R2 = Resistor [tolerance=±5% resistance=220 power=0.25 package=THT]
  S1 = Momentary Switch [package=ksa_sealed_tac_switch]
  1KΩ_Resistor = Resistor [tolerance=±5% power=0.25 resistance=220 package=THT]

nets:
  N1: Arduino.D11_PWM/MOSI, S1.1
  N2: Arduino.D12/MISO, LED1.anode
  N3: Arduino.5V, S1.4
  N4: Arduino.GND, R2.Pin_0, 1KΩ_Resistor.Pin_0
  N5: LED1.cathode, R2.Pin_1
  N6: S1.2, 1KΩ_Resistor.Pin_1
