# Fritzing sketch read_Photo_sensor (saved by Fritzing 0.9.9b)
breadboards: 1

parts:
  Arduino = Arduino Uno (Rev3)
  R1 = Resistor [tolerance=±5% resistance=10k package="2512 [SMD]"]
  R2 = PHOTOCELL [package=photocell-kit]

nets:
  N1: Arduino.A0, R1.Pin_1, R2.P$2
  N2: Arduino.5V, R2.P$1
  N3: Arduino.GND, R1.Pin_0
