# Fritzing sketch read_resistor_bb (saved by Fritzing 0.9.9b)
breadboards: 1

parts:
  Arduino = Arduino Uno (Rev3)
  R3 = Rotary Potentiometer (Small) [maximum_resistance=100kΩ package=THT]

nets:
  N1: Arduino.A0, R3.wiper
  N2: Arduino.5V, R3.leg2
  N3: Arduino.GND, R3.leg1
