# Fritzing sketch SR04_wire (saved by Fritzing 0.9.9b)

parts:
  Arduino = Arduino Uno (Rev3)
  Part1 = SRF05 Ultrasonic Rangefinder

nets:
  N1: Arduino.D8, Part1.Trig
  N2: Arduino.D9_PWM, Part1.Echo
  5V: Arduino.5V, Part1.VCC
  GND: Arduino.GND, Part1.GND
