# Fritzing sketch Uno_DHT11_bb (saved by Fritzing 0.9.9b)
breadboards: 1

parts:
  Arduino = Arduino Uno (Rev3)
  DHT12 = DHT11 Humitidy and Temperature Sensor
  R6 = Resistor [tolerance=±5% resistance=10k package="0402 [SMD]"]

nets:
  N1: Arduino.D2, R6.Pin_0
  5V: Arduino.5V, DHT12.VDD
  GND: Arduino.GND, DHT12.GND
  N2: DHT12.DATA, R6.Pin_1

custom parts:
  DHT11 Humitidy and Temperature Sensor: DHT11 Humidity and Temperature Sensor
