# Fritzing sketch Uno_DHT11_module (saved by Fritzing 0.9.9b)

parts:
  Arduino = Arduino Uno (Rev3)
  DHT11_1 = DHT11 module

nets:
  N1: Arduino.D2, DHT11_1.DATA
  5V: Arduino.5V, DHT11_1.VCC
  GND: Arduino.GND, DHT11_1.GND

custom parts:
  DHT11 module: DHT11 black pcb module
