# Fritzing sketch Servo_motor_capacitor_bb (saved by Fritzing 0.9.3b)
breadboards: 1

parts:
  Arduino = Arduino Uno (Rev3)  # not connected
  J1 = Basic Servo
  C1 = Electrolytic Capacitor [capacitance=1µF package="100 mil [THT, electrolytic]"]

nets:
  N1: J1.gnd, C1.-
  N2: J1.vcc, C1.+
