# Fritzing sketch Servo_motor_wire (saved by Fritzing 0.9.9b)

parts:
  Arduino = Arduino Uno (Rev3)
  J1 = Basic Servo

nets:
  N1: Arduino.D2, J1.pulse
  5V: Arduino.5V, J1.vcc
  GND: Arduino.GND, J1.gnd
