# Fritzing sketch _01_11_7segment_bb (saved by Fritzing 0.9.3b)
breadboards: 1

parts:
  Arduino = Arduino Uno (Rev3)
  U1 = 7-SEGMENT-DISPLAY [package=7-segment-display]
  R1 = Resistor [tolerance=±5% resistance=220 package=THT]

nets:
  N1: Arduino.D8, U1.G
  N2: Arduino.D9_PWM, U1.E
  N3: Arduino.D2, U1.G2
  N4: Arduino.D3_PWM, U1.A
  N5: Arduino.D4, U1.DP
  N6: Arduino.D5_PWM, U1.B
  N7: Arduino.D6_PWM, U1.G1
  N8: Arduino.D7, U1.D
  N9: Arduino.GND, U1.C, R1.Pin_0
  N10: U1.F, R1.Pin_1
