# Fritzing sketch _01_11_7segment_74HC595_bb (saved by Fritzing 0.9.3b)
breadboards: 1

parts:
  Arduino = Arduino Uno (Rev3)
  U1 = 7-SEGMENT-DISPLAY [package=7-segment-display]
  R1 = Resistor [tolerance=±5% resistance=220 package=THT]
  U2 = 74HC595 [package="DIP16 [THT]"]
  R2 = Resistor [tolerance=±5% resistance=220 package=THT]
  R3 = Resistor [tolerance=±5% resistance=220 package=THT]
  R4 = Resistor [tolerance=±5% resistance=220 package=THT]
  R5 = Resistor [tolerance=±5% resistance=220 package=THT]
  R6 = Resistor [tolerance=±5% resistance=220 package=THT]
  R7 = Resistor [tolerance=±5% resistance=220 package=THT]
  R8 = Resistor [tolerance=±5% resistance=220 package=THT]

nets:
  N1: Arduino.D10_PWM/SS, U2.DS
  N2: Arduino.D11_PWM/MOSI, U2.ST_CP
  N3: Arduino.D12/MISO, U2.SH_CP
  5V: Arduino.5V, U2.MR, U2.VCC
  GND: Arduino.GND, U1.F, U2.GND, U2.OE
  N4: U1.E, R1.Pin_1
  N5: U1.D, R5.Pin_1
  N6: U1.G1, R6.Pin_1
  N7: U1.DP, R8.Pin_0
  N8: U1.B, R7.Pin_0
  N9: U1.A, R4.Pin_0
  N10: U1.G2, R3.Pin_0
  N11: U1.G, R2.Pin_1
  N12: R1.Pin_0, U2.Q6
  N13: U2.Q1, R4.Pin_1
  N14: U2.Q2, R8.Pin_1
  N15: U2.Q4, R5.Pin_0
  N16: U2.Q5, R2.Pin_0
  N17: U2.Q7, R7.Pin_1
  N18: U2.Q0, R3.Pin_1
