# Fritzing sketch _01_12_Piezo (saved by Fritzing 0.9.3b)
breadboards: 1

parts:
  Arduino = Arduino Uno (Rev3)
  R5 = Resistor [tolerance=±5% resistance=220 package=THT]
  J1 = Piezo Speaker

nets:
  N1: Arduino.D8, R5.Pin_1
  N2: Arduino.GND, J1.pin1
  N3: R5.Pin_0, J1.pin2
