# Fritzing sketch _01_13_DS1302-RTC-module_wire (saved by Fritzing 0.9.3b)

parts:
  Arduino = Arduino Uno (Rev3)
  MH-Real-Time_Clock_Module_3 = RTC_DS1302_module

nets:
  N1: Arduino.D2, MH-Real-Time_Clock_Module_3.RST
  N2: Arduino.D3_PWM, MH-Real-Time_Clock_Module_3.DAT
  N3: Arduino.D4, MH-Real-Time_Clock_Module_3.CLK
  5V: Arduino.5V, MH-Real-Time_Clock_Module_3.VCC
  GND: Arduino.GND, MH-Real-Time_Clock_Module_3.GND

custom parts:
  RTC_DS1302_module: Arduino module DS1302 SPI Real Time Clock
