# Fritzing sketch _01_14_PS2_joystick_module_bb (saved by Fritzing 0.9.3b)
breadboards: 1

parts:
  Arduino = Arduino Uno (Rev3)
  Part1 = Thumb Joystick

nets:
  N1: Arduino.A0, Part1.VERT
  N2: Arduino.A1, Part1.HORZ
  N3: Arduino.D2, Part1.SEL
  5V: Arduino.5V, Part1.VCC
  GND: Arduino.GND, Part1.GND
