# Fritzing sketch _01_16_1602_wIC_module (saved by Fritzing 0.9.3b)
breadboards: 1

parts:
  Onderdeel2 = Arduino Uno (Rev3)
  LCD2 = LCD screen
  LCM1602_IIC2 = LCM1602 IIC [part_number="LCM1602 IIC" chip_label="LCM1602 IIC" package="DIP (Dual Inline) [THT]"]

nets:
  N1: Onderdeel2.A4/SDA, LCM1602_IIC2.SDA
  N2: Onderdeel2.A5/SCL, LCM1602_IIC2.SCL
  5V: Onderdeel2.5V, LCM1602_IIC2.VCC
  GND: Onderdeel2.GND, LCM1602_IIC2.GND
  VSS: LCD2.VSS, LCM1602_IIC2.VSS
  VDD: LCD2.VDD, LCM1602_IIC2.VDD
  N3: LCD2.V0, LCM1602_IIC2.V0
  N4: LCD2.RS, LCD2.R/W, LCD2.E, LCD2.DB0, LCD2.DB1, LCM1602_IIC2.RS, LCM1602_IIC2.RW, LCM1602_IIC2.E, LCM1602_IIC2.D0, LCM1602_IIC2.D1
  N5: LCD2.DB2, LCM1602_IIC2.D2
  N6: LCD2.DB3, LCM1602_IIC2.D3
  N7: LCD2.DB4, LCM1602_IIC2.D4
  N8: LCD2.DB5, LCM1602_IIC2.D5
  N9: LCD2.DB6, LCM1602_IIC2.D6
  N10: LCD2.DB7, LCM1602_IIC2.D7
  N11: LCD2.LED+, LCM1602_IIC2.A
  N12: LCD2.LED-, LCM1602_IIC2.K
  N13: LCM1602_IIC2.LED_A, LCM1602_IIC2.LED_B

custom parts:
  LCM1602 IIC: I2C-Module to use a 1602 or 2004 LCD on with the wire.h libory Serial LCD Modul
