# Fritzing sketch 01_19_Sound-Sensor_bb (saved by Fritzing 0.9.10b)
circuit board: 8.46667cm x 5.64444cm
breadboards: 1

parts:
  Onderdeel2 = Arduino Uno (Rev3)
  U2 = ESP8266 WiFi Module [part_number=ESP8266]
  Componente3 = Breakout Board for Electret Microphone  # not connected

nets:
  GND: Onderdeel2.GND, Onderdeel2.D1/TX, U2.GND, U2.TXD
  5V: Onderdeel2.D0/RX, Onderdeel2.5V, U2.RXD, U2.VCC, U2.GPIO_2, U2.CH_PD
  N1: U2.GPIO_0, U2.RST

custom parts:
  ESP8266 WiFi Module: Generic WiFi Module based on the ESP8266 with onboard PCB antenna and UART communications
