# Fritzing sketch Servo_motor_Resistor_capacitor_bb (saved by Fritzing 0.9.3b)
breadboards: 1

parts:
  Arduino = Arduino Uno (Rev3)
  J1 = Basic Servo
  C1 = Electrolytic Capacitor [capacitance=1µF package="100 mil [THT, electrolytic]"]
  R4 = Rotary Potentiometer (Small) [maximum_resistance=100kΩ package=THT]

nets:
  N1: Arduino.A0, R4.wiper
  5V: Arduino.5V, J1.vcc, J1.pulse, C1.+, R4.leg2
  GND: Arduino.GND, J1.gnd, C1.-, R4.leg1
